# Fritzing sketch LCD-Tape-Measure (saved by Fritzing 0.9.3b)
breadboards: 1

parts:
  Part1 = Arduino Uno (Rev3)
  LCD1 = LCD screen
  R1 = Resistor [tolerance=±5% resistance=220 package=THT]
  R2 = Trimmer Potentiometer [maximum_resistance=10kΩ package=THT]
  hc-sr1 = hc-sr04

nets:
  N1: Part1.D11_PWM/MOSI, LCD1.E
  N2: Part1.D12/MISO, LCD1.RS
  GND: Part1.GND, LCD1.VSS, LCD1.R/W, LCD1.LED-, R2.leg1, hc-sr1.GND
  N3: Part1.D2, LCD1.DB7
  N4: Part1.D3_PWM, LCD1.DB6
  N5: Part1.D4, LCD1.DB5
  N6: Part1.D5_PWM, LCD1.DB4
  N7: Part1.D7, hc-sr1.Trig, hc-sr1.Echo
  5V: Part1.5V, LCD1.VDD, R1.Pin_1, R2.leg2, hc-sr1.VCC
  N8: LCD1.V0, R2.wiper
  N9: LCD1.LED+, R1.Pin_0
